# Fritzing sketch lidar_scanner_breadboard (saved by Fritzing 0.9.9b)
circuit board: 8.85467cm x 13.762cm
circuit board: 7.67839cm x 10.1219cm
breadboards: 1

parts:
  Power_plug1 = Power plug
  Pololu_A1 = Pololu A4988 [package=SO16]
  M7 = Stepper Motor - Bipolar
  Part3 = Arduino Nano (Rev3.0)
  C3 = Capacitor Polarized [package=cpol-radial-100uf-25v]

nets:
  GND: Power_plug1.GND, Pololu_A1.GND, Part3.GND, C3.-
  VCC: Power_plug1.VCC, Part3.VIN
  N1: Pololu_A1.ENABLE, Part3.D12/MISO
  N2: Pololu_A1.RESET, Pololu_A1.SLEEP
  N3: Pololu_A1.STEP, Part3.D11/MOSI
  N4: Pololu_A1.DIR, Part3.D10
  VDD: Pololu_A1.VDD, Part3.5V
  N5: Pololu_A1.1B, M7.D
  N6: Pololu_A1.1A, M7.B
  N7: Pololu_A1.2A, M7.C
  N8: Pololu_A1.2B, M7.A
  N9: Pololu_A1.VMOT, C3.+
